# Fritzing sketch ble_dimmer (saved by Fritzing 0.9.2b)

parts:
  Part1 = Arduino Pro Mini v13
  U1 = Optocoupler [package=THT]
  D1 = Rectifier Diode [package="Melf DO-213 AA [SMD]"]
  D2 = Rectifier Diode [package="Melf DO-213 AA [SMD]"]
  D3 = Rectifier Diode [package="Melf DO-213 AA [SMD]"]
  D4 = Rectifier Diode [package="Melf DO-213 AA [SMD]"]
  R1 = Resistor [tolerance=±5% resistance=91k package="2512 [SMD]"]
  R2 = Resistor [tolerance=±5% resistance=91k package="2512 [SMD]"]
  R3 = Resistor [tolerance=±5% resistance=10k package="0805 [SMD]"]
  R4 = Resistor [tolerance=±5% resistance=220 package="0805 [SMD]"]
  LED1 = LEDs [package=led10mm]
  U3 = MOC3031-M [package=dil06]
  R5 = Resistor [tolerance=±5% resistance=220 package="0805 [SMD]"]
  U4 = TRIAC [package=to-92]
  R7 = Resistor [tolerance=±5% resistance=220 package="0805 [SMD]"]
  R6 = Resistor [tolerance=±5% resistance=220 package="0805 [SMD]"]
  LED2 = LEDs [package=led10mm]
  U5 = MOC3031-M [package=dil06]
  U6 = TRIAC [package=to-92]
  J2 = Screw terminal - 2 pins [part_number=dim1-2 package=THT]
  J3 = Screw terminal - 2 pins [part_number="AC 220V" package=THT]
  HLK-PM1 = HLK-PM01
  Part2 = Bluetooth Mate Silver

nets:
  GND: Part1.GND, U1.Pin_4, U3.2, U5.2, HLK-PM1.-Vo, Part2.GND
  N1: Part1.RAW, HLK-PM1.+Vo
  N2: Part1.D11_PWM/MOSI, Part2.TX_5V
  N3: Part1.D10_PWM/SS, Part2.RX_5V
  N4: Part1.D5_PWM, R6.Pin_0
  N5: Part1.D3_PWM, R4.Pin_0
  N6: Part1.D2, U1.Pin_5, R3.Pin_0
  N7: U1.Pin_1, D2.cathode, D4.cathode
  N8: U1.Pin_2, D1.anode, D3.anode
  N9: D1.cathode, D2.anode, R1.Pin_1
  N10: D3.cathode, D4.anode, R2.Pin_1
  N11: R1.Pin_0, R5.Pin_1, U4.M2, R7.Pin_1, U6.M2, J3.pin1, HLK-PM1.AC#1
  N12: R2.Pin_0, J3.pin2, HLK-PM1.AC#0
  N13: R4.Pin_1, LED1.A
  N14: LED1.C, U3.1
  N15: U3.4, U4.G
  N16: U3.6, R5.Pin_0
  N17: U4.M1, J2.pin2
  N18: R7.Pin_0, U5.6
  N19: R6.Pin_1, LED2.A
  N20: LED2.C, U5.1
  N21: U5.4, U6.G
  N22: U6.M1, J2.pin1
